// Logisim project control-logic.circ as structural Verilog: 1 circuit, main circuit control_logic
module control_logic (
  input  [31:0] Instruction,
  input  BrEq,
  input  BrLt,
  output PCSel,
  output RegWEn,
  output [2:0] ImmSel,
  output BrUn,
  output ASel,
  output BSel,
  output [3:0] ALUSel,
  output MemRW,
  output [1:0] WBSel
);

  wire comparator_2_eq, RItype;

  Comparator #(.width(5)) comparator_1 (.a(Instruction[6:2]), .b(5'b00100), .eq(RItype));  // open: gt, lt
  or or_1 (RegWEn, 1'b0, RItype);
  or or_2 (BSel, 1'b0, RItype);
  Comparator #(.mode("unsigned"), .width(3)) comparator_2 (
    .a(Instruction[14:12]), .b(3'b101), .eq(comparator_2_eq));  // open: gt, lt
  or or_3 (WBSel[0], RItype, 1'b0);
  or or_4 (WBSel[1], 1'b0, 1'b0);
  and and_1 (ALUSel[3], Instruction[30], RItype, comparator_2_eq);
  Priority_Encoder priority_encoder_1 (
    .in0(RItype), .out(ImmSel));  // open: in1, in2, in3, in4, in5, in6, in7, en_in, gs, en_out

  assign ALUSel[2:0] = Instruction[14:12];
  assign ASel = 1'b0;
  assign BrUn = 1'b0;
  assign MemRW = 1'b0;
  assign PCSel = 1'b0;

  // Other names for the same wires on the sheet: func3[2:0] = Instruction[14:12]; opcode[4:0] = Instruction[6:2];
  //   func7 = Instruction[30]

  // Notes on the sheet:
  //   INPUTS to your circuit
  //   DON'T CHANGE THE LOCATIONS OF THE INPUTS AND OUTPUTS!
  //   OUTPUT from your circuit
endmodule
